# Fritzing sketch Data logger digram (saved by Fritzing 0.9.4)

parts:
  microSD = MicroSD Card Module
  SHT31_T&H_Sensor = HTU21D Breakout
  HC-05 = Bluetooth HC-05 Macho
  DS3231 = ZS-042 RTC Module
  BMP180_AirPressure_Sensor = Barometric Pressure Sensor - BMP180 Breakout (GY-68)
  PCA9306 = PCA9306 [package=psop-8]
  Part5 = Arduino Mega 2560 (Rev3)
  Power_plug_<9V = Power plug
  LCD1 = TFT 1.8 inch 160x128 w SD
  SG1 = Buzzer 12mm [part_number=COM-07950 package=buzzer-12mm-ns]
  (36V-10V)_to_9V = RioRand LM2596
  Power_plug_10V-36V = Power plug

nets:
  N1: microSD.CS, Part5.D6_PWM
  N2: SHT31_T&H_Sensor.SCL, BMP180_AirPressure_Sensor.SCL, PCA9306.SCL1
  N3: SHT31_T&H_Sensor.SDA, BMP180_AirPressure_Sensor.SDA, PCA9306.SDA1
  GND: SHT31_T&H_Sensor.GND, BMP180_AirPressure_Sensor.GND, PCA9306.GND#3
  3.3V: SHT31_T&H_Sensor.3.3V, BMP180_AirPressure_Sensor.VCC, PCA9306.VREF1
  N4: HC-05.TXD, Part5.D11_PWM
  N5: HC-05.RXD, Part5.D12_PWM
  VCC: HC-05.VCC, DS3231.VCC, PCA9306.VREF2, Part5.5V, LCD1.pin_1
  GND_2: HC-05.GND, DS3231.GND, PCA9306.GND#7, Part5.GND, Power_plug_<9V.GND, LCD1.pin2, SG1.2, (36V-10V)_to_9V.Pin_4
  N6: DS3231.SDA, PCA9306.SDA2, Part5.D20/SDA, Part5.SDA
  N7: DS3231.SCL, PCA9306.SCL2, Part5.D21/SCL, Part5.SCL
  N8: Part5.D10_PWM, LCD1.pin3
  N9: Part5.D9_PWM, LCD1.pin4
  N10: Part5.D8_PWM, LCD1.pin_5
  N11: Part5.3V3, LCD1.pin_8
  VIN: Part5.VIN, Power_plug_<9V.VCC, (36V-10V)_to_9V.Pin_3
  N12: Part5.D7_PWM, SG1.1
  N13: Part5.D52, LCD1.pin_7
  N14: Part5.D53, LCD1.pin_6
  N15: (36V-10V)_to_9V.Pin_1, Power_plug_10V-36V.VCC
  N16: (36V-10V)_to_9V.Pin_2, Power_plug_10V-36V.GND

notes:
  sensor cable (i2c)
  R1 old
  low cost
  R2 new
  expensive
  OR

custom parts:
  HTU21D Breakout: This is a breadboard friendly breakout board for the Measurement Specialties high-precision, low-power digital humidity sensor.
  PCA9306: Bidirectional I2C level shifter. NOT compatible with all available part number pinout schemes- DOUBLE CHECK!!!
  TFT 1.8 inch 160x128 w SD: This is a generic 1.8 tft spi lcd display available on ebay and others. The 1.8" display has 128x160 color pixels.
  Buzzer 12mm: Buzzer 12mm Spark Fun Electronics SKU : Comp-Buzzer Through hole This is a small 12mm round speaker that operates around the audible 2kHz range. You can use these speakers to create simple music or user interfaces. This is not a true piezoelectric speaker but behaves similarly. Instead of a piezoelectric crystal that vibrates with an electric current, this tiny speaker uses an electromagnet to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
